// Logisim project ALU.circ as structural Verilog: 8 circuits, main circuit main
module main (
);

  RegisterFile registerfile_1 ();  // open: R1, R2, WE, CLK, WD, W, RD1, RD2
  ALU alu_1 ();  // open: A, B, OP, V, N, Z, C, R
  ROM #(.addrWidth(12), .dataWidth(16)) Program ();  // open: addr, data
endmodule

module fourBitCarryLookaheadAdder (
  input  [3:0] A,
  input  [3:0] B,
  input  M,
  output Cout,
  output [3:0] R
);

  wire A0B0_out, A1B1_out, A2B2_out, A3B3_out, and_1_out, and_2_out, and_3_out, and_4_out, and_5_out,
       and_6_out, and_7_out, and_8_out, and_9_out, and_10_out, C1_out, C2_out, C3_out, xor_1_out, xor_2_out,
       xor_3_out, xor_4_out;
  wire [3:0] multiplexer_1_out, not_1_out;

  Multiplexer #(.width(4)) multiplexer_1 (.in0(B), .in1(not_1_out), .out(multiplexer_1_out), .sel(M));
  assign not_1_out = ~B;  // NOT_Gate not_1, 4 bits wide
  and A0B0 (A0B0_out, multiplexer_1_out[0], A[0]);
  xor xor_1 (xor_1_out, multiplexer_1_out[3], A[3]);
  xor xor_2 (xor_2_out, multiplexer_1_out[2], A[2]);
  xor xor_3 (xor_3_out, multiplexer_1_out[1], A[1]);
  xor xor_4 (xor_4_out, multiplexer_1_out[0], A[0]);
  and A1B1 (A1B1_out, multiplexer_1_out[1], A[1]);
  and and_1 (and_1_out, M, xor_4_out, xor_3_out);
  and and_2 (and_2_out, A0B0_out, xor_3_out);
  or C2 (C2_out, A1B1_out, and_1_out, and_2_out);
  and and_3 (and_3_out, M, xor_4_out);
  and A3B3 (A3B3_out, multiplexer_1_out[3], A[3]);
  and and_4 (and_4_out, M, xor_4_out, xor_3_out, xor_2_out, xor_1_out);
  and and_5 (and_5_out, A0B0_out, xor_3_out, xor_2_out, xor_1_out);
  and and_6 (and_6_out, A1B1_out, xor_2_out, xor_1_out);
  and and_7 (and_7_out, A2B2_out, xor_1_out);
  and A2B2 (A2B2_out, multiplexer_1_out[2], A[2]);
  and and_8 (and_8_out, M, xor_4_out, xor_3_out, xor_2_out);
  and and_9 (and_9_out, A0B0_out, xor_3_out, xor_2_out);
  and and_10 (and_10_out, A1B1_out, xor_2_out);
  or C1 (C1_out, and_3_out, A0B0_out);
  or C3 (C3_out, A2B2_out, and_8_out, and_9_out, and_10_out);
  or C4 (Cout, A3B3_out, and_4_out, and_5_out, and_6_out, and_7_out);
  xor R3 (R[3], xor_1_out, C3_out);
  xor R2 (R[2], xor_2_out, C2_out);
  xor R1 (R[1], xor_3_out, C1_out);
  xor R0 (R[0], xor_4_out, M);

  // Notes on the sheet:
  //   Carry Bits
  //   Addition for R0-R3
endmodule

module twelveBitRippleCarryAdder (
  input  M,
  input  [11:0] A,
  input  [11:0] B,
  output Cout,
  output [11:0] R
);

  wire CLA0_cout, CLA1_cout, xor_1_out, xor_2_out;
  wire [3:0] multiplexer_1_out, multiplexer_2_out, not_1_out, not_2_out;

  fourBitCarryLookaheadAdder CLA0 (.A(A[3:0]), .B(B[3:0]), .M(M), .Cout(CLA0_cout), .R(R[3:0]));
  assign not_1_out = ~B[7:4];  // NOT_Gate not_1, 4 bits wide
  Multiplexer #(.width(4)) multiplexer_1 (.in0(B[7:4]), .in1(not_1_out), .out(multiplexer_1_out), .sel(xor_1_out));
  xor xor_1 (xor_1_out, CLA0_cout, M);
  fourBitCarryLookaheadAdder CLA1 (.A(A[7:4]), .B(multiplexer_1_out), .M(CLA0_cout), .Cout(CLA1_cout), .R(R[7:4]));
  assign not_2_out = ~B[11:8];  // NOT_Gate not_2, 4 bits wide
  xor xor_2 (xor_2_out, CLA1_cout, M);
  Multiplexer #(.width(4)) multiplexer_2 (.in0(B[11:8]), .in1(not_2_out), .out(multiplexer_2_out), .sel(xor_2_out));
  fourBitCarryLookaheadAdder CLA2 (.A(A[11:8]), .B(multiplexer_2_out), .M(CLA1_cout), .Cout(Cout), .R(R[11:8]));

  // Notes on the sheet:
  //   A3-A0 & B3-B0
  //   I have to invert the value of every 4 bits of B to invert the subtraction to use only one input for Mode/Carry in. Otherwise, this is a simple ripple-carry adder.
  //   A7-A4 & B7-B4
  //   A11-A8 & B11-B8
endmodule

module ALU (
  input  [11:0] A,
  input  [11:0] B,
  input  [2:0] OP,
  output V,
  output N,
  output Z,
  output C,
  output [11:0] R
);

  wire AddO_out, and_2_out, and_3_out, and_4_out, and_5_out, and_6_out, nor_1_out, nor_2_out, not_2_out,
       not_3_out, not_4_out, or_2_out, or_3_out, SubO_out;
  wire [11:0] Adder_Subtractor_r, and_1_out, not_1_out, or_1_out;

  assign not_1_out = ~A;  // NOT_Gate not_1, 12 bits wide
  not not_2 (not_2_out, B[11]);
  not not_3 (not_3_out, A[11]);
  assign and_1_out = A & B;  // AND_Gate and_1, 12 bits wide
  assign or_1_out = A | B;  // OR_Gate or_1, 12 bits wide
  not not_4 (not_4_out, N);
  and and_2 (and_2_out, nor_1_out, OP[0]);
  nor nor_1 (nor_1_out, OP[2], OP[1]);
  twelveBitRippleCarryAdder Adder_Subtractor (.M(OP[0]), .A(A), .B(B), .Cout(C), .R(Adder_Subtractor_r));
  and and_3 (and_3_out, B[11], A[11], not_4_out);
  and and_4 (and_4_out, not_2_out, not_3_out, N);
  and and_5 (and_5_out, B[11], not_3_out, not_4_out);
  and and_6 (and_6_out, not_2_out, A[11], N);
  or or_2 (or_2_out, and_3_out, and_4_out);
  and AddO (AddO_out, or_2_out, nor_2_out);
  or or_3 (or_3_out, and_5_out, and_6_out);
  nor nor_2 (nor_2_out, OP[2], OP[1], OP[0]);
  and SubO (SubO_out, or_3_out, and_2_out);
  Multiplexer #(.select(3), .width(12)) multiplexer_1 (
    .in0(Adder_Subtractor_r), .in1(Adder_Subtractor_r), .in2(and_1_out), .in3(or_1_out), .in4(not_1_out),
    .in5({12{1'b0}}), .in6({12{1'b0}}), .in7({12{1'b0}}), .out({N, R[10:0]}), .sel(OP));
  or or_4 (V, AddO_out, SubO_out);
  NotExactlyOne xnor_1 (
    .out(Z), .in0(N), .in1(R[10]), .in2(R[9]), .in3(R[8]), .in4(R[7]), .in5(R[6]), .in6(R[5]), .in7(R[4]),
    .in8(R[3]), .in9(R[2]), .in10(R[1]), .in11(R[0]));

  assign R[11] = N;

  // Notes on the sheet:
  //   B0-11
  //   A0-11
  //   These top two and gates + or gate is Addition Overflow. Checks if output sign is different from operands.
  //   Carry Flag
  //   Negative Flag
  //   0 - Add
  //   2 - And
  //   3 - Or
  //   4 - Not
  //   Connect extra op codes to ground for 0. Gives me consistent outputs for testing bad op codes.
  //   Overflow Flag
  //   R0-11
  //   1 - Subtract
  //   Zero Flag
endmodule

module RegisterFile (
  input  [2:0] R1,
  input  [2:0] R2,
  input  WE,
  input  CLK,
  input  [11:0] WD,
  input  [2:0] W,
  output [11:0] RD1,
  output [11:0] RD2
);

  wire and_1_out, and_2_out, and_3_out, and_4_out, and_5_out, and_6_out, and_7_out, and_8_out,
       decoder_1_out0, decoder_1_out1, decoder_1_out2, decoder_1_out3, decoder_1_out4, decoder_1_out5,
       decoder_1_out6, decoder_1_out7;
  wire [11:0] Reg0_q, Reg1_q, Reg2_q, Reg3_q, Reg4_q, Reg5_q, Reg6_q, Reg7_q;

  Decoder #(.select(3)) decoder_1 (
    .out0(decoder_1_out0), .out1(decoder_1_out1), .out2(decoder_1_out2), .out3(decoder_1_out3),
    .out4(decoder_1_out4), .out5(decoder_1_out5), .out6(decoder_1_out6), .out7(decoder_1_out7), .sel(W));  // open: en
  and and_1 (and_1_out, decoder_1_out0, WE);
  and and_2 (and_2_out, decoder_1_out1, WE);
  and and_3 (and_3_out, decoder_1_out2, WE);
  and and_4 (and_4_out, decoder_1_out3, WE);
  and and_5 (and_5_out, decoder_1_out4, WE);
  and and_6 (and_6_out, decoder_1_out5, WE);
  and and_7 (and_7_out, decoder_1_out6, WE);
  and and_8 (and_8_out, decoder_1_out7, WE);
  twelveBitRegister Reg0 (.WE(and_1_out), .CLK(CLK), .D(WD), .Q(Reg0_q));  // open: QNot
  twelveBitRegister Reg1 (.WE(and_2_out), .CLK(CLK), .D(WD), .Q(Reg1_q));  // open: QNot
  twelveBitRegister Reg2 (.WE(and_3_out), .CLK(CLK), .D(WD), .Q(Reg2_q));  // open: QNot
  twelveBitRegister Reg3 (.WE(and_4_out), .CLK(CLK), .D(WD), .Q(Reg3_q));  // open: QNot
  twelveBitRegister Reg4 (.WE(and_5_out), .CLK(CLK), .D(WD), .Q(Reg4_q));  // open: QNot
  twelveBitRegister Reg5 (.WE(and_6_out), .CLK(CLK), .D(WD), .Q(Reg5_q));  // open: QNot
  twelveBitRegister Reg6 (.WE(and_7_out), .CLK(CLK), .D(WD), .Q(Reg6_q));  // open: QNot
  twelveBitRegister Reg7 (.WE(and_8_out), .CLK(CLK), .D(WD), .Q(Reg7_q));  // open: QNot
  Multiplexer #(.select(3), .width(12)) multiplexer_1 (
    .in0(Reg0_q), .in1(Reg1_q), .in2(Reg2_q), .in3(Reg3_q), .in4(Reg4_q), .in5(Reg5_q), .in6(Reg6_q),
    .in7(Reg7_q), .out(RD1), .sel(R1));
  Multiplexer #(.select(3), .width(12)) multiplexer_2 (
    .in0(Reg0_q), .in1(Reg1_q), .in2(Reg2_q), .in3(Reg3_q), .in4(Reg4_q), .in5(Reg5_q), .in6(Reg6_q),
    .in7(Reg7_q), .out(RD2), .sel(R2));
endmodule

module DLatch (
  input  CLK,
  input  D,
  output Q,
  output QNot
);

  wire and_1_out, and_2_out, not_1_out;

  not not_1 (not_1_out, D);
  and and_1 (and_1_out, CLK, not_1_out);
  and and_2 (and_2_out, CLK, D);
  nor nor_1 (Q, and_1_out, QNot);
  nor nor_2 (QNot, Q, and_2_out);

  // Notes on the sheet:
  //   This is the simplest building block of the Register
endmodule

module DFlipFlop (
  input  CLK,
  input  D,
  output Q,
  output QNot
);

  wire not_1_out, Qbefore_q;

  not not_1 (not_1_out, CLK);
  DLatch Qbefore (.CLK(not_1_out), .D(D), .Q(Qbefore_q));  // open: QNot
  DLatch Qafter (.CLK(CLK), .D(Qbefore_q), .Q(Q), .QNot(QNot));

  // Notes on the sheet:
  //   This latch ensures it only gets set on clock edge
endmodule

module twelveBitRegister (
  input  WE,
  input  CLK,
  input  [11:0] D,
  output [11:0] Q,
  output [11:0] QNot
);

  wire and_1_out;

  and and_1 (and_1_out, WE, CLK);
  DFlipFlop B11 (.CLK(and_1_out), .D(D[11]), .Q(Q[11]), .QNot(QNot[11]));
  DFlipFlop B10 (.CLK(and_1_out), .D(D[10]), .Q(Q[10]), .QNot(QNot[10]));
  DFlipFlop B9 (.CLK(and_1_out), .D(D[9]), .Q(Q[9]), .QNot(QNot[9]));
  DFlipFlop B8 (.CLK(and_1_out), .D(D[8]), .Q(Q[8]), .QNot(QNot[8]));
  DFlipFlop B7 (.CLK(and_1_out), .D(D[7]), .Q(Q[7]), .QNot(QNot[7]));
  DFlipFlop B6 (.CLK(and_1_out), .D(D[6]), .Q(Q[6]), .QNot(QNot[6]));
  DFlipFlop B5 (.CLK(and_1_out), .D(D[5]), .Q(Q[5]), .QNot(QNot[5]));
  DFlipFlop B4 (.CLK(and_1_out), .D(D[4]), .Q(Q[4]), .QNot(QNot[4]));
  DFlipFlop B3 (.CLK(and_1_out), .D(D[3]), .Q(Q[3]), .QNot(QNot[3]));
  DFlipFlop B2 (.CLK(and_1_out), .D(D[2]), .Q(Q[2]), .QNot(QNot[2]));
  DFlipFlop B1 (.CLK(and_1_out), .D(D[1]), .Q(Q[1]), .QNot(QNot[1]));
  DFlipFlop B0 (.CLK(and_1_out), .D(D[0]), .Q(Q[0]), .QNot(QNot[0]));

  // Notes on the sheet:
  //   This is simply 12 flip flops that are only written to when Write Enable (WE) and CLK are both true
endmodule
