// Logisim project NISC_CPU.circ as structural Verilog
module main (
);

  wire nisc_cpu_1_c, nisc_cpu_1_n, nisc_cpu_1_v, nisc_cpu_1_z;
  wire [3:0] IM_data, IM_data_2, IM_data_3, nisc_cpu_1_im_address_2;
  wire [7:0] nisc_cpu_1_im_address;
  wire [11:0] nisc_cpu_1_or0;

  ROM #(.addrWidth(9), .dataWidth(12)) IM (
    .addr({nisc_cpu_1_im_address_2[0], nisc_cpu_1_im_address}), .data({IM_data_3, IM_data_2, IM_data}));
  NISC_CPU nisc_cpu_1 (
    .IM_Data({IM_data_3, IM_data_2, IM_data}),
    .IM_Address({nisc_cpu_1_im_address_2[0], nisc_cpu_1_im_address}), .N(nisc_cpu_1_n), .Z(nisc_cpu_1_z),
    .C(nisc_cpu_1_c), .V(nisc_cpu_1_v), .OR0(nisc_cpu_1_or0));
  LED led_1 (.in(nisc_cpu_1_n));
  LED led_2 (.in(nisc_cpu_1_z));
  LED led_3 (.in(nisc_cpu_1_c));
  LED led_4 (.in(nisc_cpu_1_v));
  Hex_Digit_Display hex_digit_display_1 (.value(nisc_cpu_1_im_address_2));  // open: dp
  Hex_Digit_Display hex_digit_display_2 (.value(nisc_cpu_1_im_address[7:4]));  // open: dp
  Hex_Digit_Display hex_digit_display_3 (.value(nisc_cpu_1_or0[11:8]));  // open: dp
  Hex_Digit_Display hex_digit_display_4 (.value(nisc_cpu_1_im_address[3:0]));  // open: dp
  Hex_Digit_Display hex_digit_display_5 (.value(IM_data_3));  // open: dp
  Hex_Digit_Display hex_digit_display_6 (.value(nisc_cpu_1_or0[7:4]));  // open: dp
  Hex_Digit_Display hex_digit_display_7 (.value(nisc_cpu_1_or0[3:0]));  // open: dp
  Hex_Digit_Display hex_digit_display_8 (.value(IM_data_2));  // open: dp
  Hex_Digit_Display hex_digit_display_9 (.value(IM_data));  // open: dp

  // Notes on the sheet:
  //   contents of IM (hex, n*v repeats v):
  //   c00 0 940 c23 21b e0a c08 c07 83f e0b c00 e0b
  //   NISC
  //   SP25-Example-Demo
  //   IM Address
  //   R0 Contents
  //   IM Data
endmodule

module RegisterFile (
  input  [2:0] RA1,
  input  [2:0] RA2,
  input  Reset,
  input  RegW,
  input  [11:0] WD3,
  input  [2:0] WA3,
  input  CLK,
  output [11:0] RD1,
  output [11:0] RD2,
  output [11:0] OR0
);

  wire and_1_out, and_2_out, and_3_out, and_4_out, and_5_out, and_6_out, and_7_out, and_8_out,
       decoder_1_out0, decoder_1_out1, decoder_1_out2, decoder_1_out3, decoder_1_out4, decoder_1_out5,
       decoder_1_out6, decoder_1_out7, or_1_out, or_2_out, or_3_out, or_4_out, or_5_out, or_6_out, or_7_out,
       or_8_out;
  wire [11:0] multiplexer_1_out, R1_q, R2_q, R3_q, R4_q, R5_q, R6_q, R7_q;

  Multiplexer #(.width(12)) multiplexer_1 (.in0(WD3), .in1({12{1'b0}}), .out(multiplexer_1_out), .sel(Reset));
  Decoder #(.select(3)) decoder_1 (
    .out0(decoder_1_out0), .out1(decoder_1_out1), .out2(decoder_1_out2), .out3(decoder_1_out3),
    .out4(decoder_1_out4), .out5(decoder_1_out5), .out6(decoder_1_out6), .out7(decoder_1_out7), .sel(WA3));  // open: en
  and and_1 (and_1_out, decoder_1_out0, RegW);
  and and_2 (and_2_out, decoder_1_out1, RegW);
  and and_3 (and_3_out, decoder_1_out2, RegW);
  and and_4 (and_4_out, decoder_1_out3, RegW);
  and and_5 (and_5_out, decoder_1_out4, RegW);
  and and_6 (and_6_out, decoder_1_out5, RegW);
  and and_7 (and_7_out, decoder_1_out6, RegW);
  and and_8 (and_8_out, decoder_1_out7, RegW);
  or or_1 (or_1_out, Reset, and_1_out);
  or or_2 (or_2_out, Reset, and_2_out);
  or or_3 (or_3_out, Reset, and_3_out);
  or or_4 (or_4_out, Reset, and_4_out);
  or or_5 (or_5_out, Reset, and_5_out);
  or or_6 (or_6_out, Reset, and_6_out);
  or or_7 (or_7_out, Reset, and_7_out);
  or or_8 (or_8_out, Reset, and_8_out);
  Register #(.width(12)) R0 (.D(multiplexer_1_out), .en(or_1_out), .clk(CLK), .Q(OR0));  // open: clr
  Register #(.width(12)) R1 (.D(multiplexer_1_out), .en(or_2_out), .clk(CLK), .Q(R1_q));  // open: clr
  Register #(.width(12)) R2 (.D(multiplexer_1_out), .en(or_3_out), .clk(CLK), .Q(R2_q));  // open: clr
  Register #(.width(12)) R3 (.D(multiplexer_1_out), .en(or_4_out), .clk(CLK), .Q(R3_q));  // open: clr
  Register #(.width(12)) R4 (.D(multiplexer_1_out), .en(or_5_out), .clk(CLK), .Q(R4_q));  // open: clr
  Register #(.width(12)) R5 (.D(multiplexer_1_out), .en(or_6_out), .clk(CLK), .Q(R5_q));  // open: clr
  Register #(.width(12)) R6 (.D(multiplexer_1_out), .en(or_7_out), .clk(CLK), .Q(R6_q));  // open: clr
  Register #(.width(12)) R7 (.D(multiplexer_1_out), .en(or_8_out), .clk(CLK), .Q(R7_q));  // open: clr
  Multiplexer #(.select(3), .width(12)) multiplexer_2 (
    .in0(OR0), .in1(R1_q), .in2(R2_q), .in3(R3_q), .in4(R4_q), .in5(R5_q), .in6(R6_q), .in7(R7_q), .out(RD1),
    .sel(RA1));
  Multiplexer #(.select(3), .width(12)) multiplexer_3 (
    .in0(OR0), .in1(R1_q), .in2(R2_q), .in3(R3_q), .in4(R4_q), .in5(R5_q), .in6(R6_q), .in7(R7_q), .out(RD2),
    .sel(RA2));

  // Notes on the sheet:
  //   Ground for reset
endmodule

module ALU (
  input  [11:0] A,
  input  [11:0] B,
  input  [2:0] ALUOP,
  output [11:0] R,
  output N,
  output Z,
  output C,
  output V
);

  wire AddO_out, and_2_out, and_3_out, and_4_out, and_5_out, and_6_out, nor_1_out, nor_2_out, not_1_out,
       not_3_out, not_4_out, or_2_out, or_3_out, SubO_out;
  wire [11:0] and_1_out, not_2_out, or_1_out, twelvebitrca_1_r;

  not not_1 (not_1_out, B[11]);
  assign and_1_out = A & B;  // AND_Gate and_1, 12 bits wide
  assign or_1_out = A | B;  // OR_Gate or_1, 12 bits wide
  assign not_2_out = ~A;  // NOT_Gate not_2, 12 bits wide
  not not_3 (not_3_out, A[11]);
  nor nor_1 (nor_1_out, ALUOP[2], ALUOP[1]);
  not not_4 (not_4_out, N);
  twelveBitRCA twelvebitrca_1 (.M(ALUOP[0]), .A(A), .B(B), .Cout(C), .R(twelvebitrca_1_r));
  and and_2 (and_2_out, B[11], A[11], not_4_out);
  and and_3 (and_3_out, not_1_out, not_3_out, N);
  and and_4 (and_4_out, B[11], not_3_out, not_4_out);
  and and_5 (and_5_out, not_1_out, A[11], N);
  and and_6 (and_6_out, nor_1_out, ALUOP[0]);
  or or_2 (or_2_out, and_2_out, and_3_out);
  or or_3 (or_3_out, and_4_out, and_5_out);
  nor nor_2 (nor_2_out, ALUOP[2], ALUOP[1], ALUOP[0]);
  and AddO (AddO_out, or_2_out, nor_2_out);
  and SubO (SubO_out, or_3_out, and_6_out);
  or or_4 (V, AddO_out, SubO_out);
  Multiplexer #(.select(3), .width(12)) multiplexer_1 (
    .in0(twelvebitrca_1_r), .in1(twelvebitrca_1_r), .in2(and_1_out), .in3(or_1_out), .in4(not_2_out),
    .in5({A[10:0], 1'b0}), .in6({1'b0, A[11:1]}), .in7({{2{A[11]}}, A[10:1]}), .out({N, R[10:0]}), .sel(ALUOP));
  nor nor_3 (Z, N, R[10], R[9], R[8], R[7], R[6], R[5], R[4], R[3], R[2], R[1], R[0]);

  assign R[11] = N;

  // Other names for the same wires on the sheet: Op[2:0] = ALUOP

  // Notes on the sheet:
  //   LSL, LSR, ASR
  //   B0-11
  //   A0-11
  //   These top two and gates + or gate is Addition Overflow. Checks if output sign is different from operands.
  //   Carry Flag
  //   Negative Flag
  //   R0-11
  //   0 - Add
  //   1 - Subtract
  //   2 - And
  //   3 - Or
  //   4 - Not
  //   Overflow Flag
  //   Zero Flag
endmodule

module NISC_CPU (
  input  [11:0] IM_Data,
  output [8:0] IM_Address,
  output N,
  output Z,
  output C,
  output V,
  output [11:0] OR0
);

  wire alu_1_c, alu_1_n, alu_1_v, alu_1_z, and_1_out, B, CLK, CVW, FlagsW, MOVC, MOVF, not_1_out, NZW, RegW,
       Reset;
  wire [2:0] controlunit_1_aluop, undriven;
  wire [11:0] ALUR, and_2_out, FlagQ, multiplexer_1_out, multiplexer_2_out, multiplexer_3_out,
       registerfile_1_rd1, registerfile_1_rd2, signextend6_1_s12, twelvebitrca_1_r;
  wire [11:9] register_1_q;

  ControlUnit controlunit_1 (
    .IWord(IM_Data), .MOVC(MOVC), .MOVF(MOVF), .RegW(RegW), .FlagsW(FlagsW), .NZW(NZW), .CVW(CVW), .B(B),
    .ALUOP(controlunit_1_aluop));
  Multiplexer #(.select(2), .width(12)) multiplexer_1 (
    .in0(ALUR), .in1(signextend6_1_s12), .in2(FlagQ), .out(multiplexer_1_out), .sel({MOVF, MOVC}));  // open: in3
  SignExtend6 signextend6_1 (.S6(IM_Data[8:3]), .S12(signextend6_1_s12));
  Hex_Digit_Display hex_digit_display_1 (.value(IM_Data[11:8]));  // open: dp
  Hex_Digit_Display hex_digit_display_2 (.value(IM_Data[7:4]));  // open: dp
  RegisterFile registerfile_1 (
    .RA1(IM_Data[5:3]), .RA2(IM_Data[8:6]), .Reset(Reset), .RegW(RegW), .WD3(multiplexer_1_out),
    .WA3(IM_Data[2:0]), .CLK(CLK), .RD1(registerfile_1_rd1), .RD2(registerfile_1_rd2), .OR0(OR0));
  Hex_Digit_Display hex_digit_display_3 (.value(IM_Data[3:0]));  // open: dp
  Clock clock_1 (.out(CLK));
  Button u_Reset (.out(Reset));
  ALU alu_1 (
    .A(registerfile_1_rd1), .B(registerfile_1_rd2), .ALUOP(controlunit_1_aluop), .R(ALUR), .N(alu_1_n),
    .Z(alu_1_z), .C(alu_1_c), .V(alu_1_v));
  Hex_Digit_Display hex_digit_display_4 (.value(OR0[11:8]));  // open: dp
  Hex_Digit_Display hex_digit_display_5 (.value(OR0[7:4]));  // open: dp
  Hex_Digit_Display hex_digit_display_6 (.value(OR0[3:0]));  // open: dp
  Hex_Digit_Display hex_digit_display_7 (.value({undriven, IM_Address[8]}));  // open: dp
  Hex_Digit_Display hex_digit_display_8 (.value(IM_Address[7:4]));  // open: dp
  not not_1 (not_1_out, Z);
  FlagsReg flagsreg_1 (
    .N(alu_1_n), .Z(alu_1_z), .C(alu_1_c), .V(alu_1_v), .D12(registerfile_1_rd1), .NZW(NZW), .CVW(CVW),
    .FlagsW(FlagsW), .CLK(CLK), .Reset(Reset), .Nq(N), .Zq(Z), .Cq(C), .Vq(V), .Q12(FlagQ));
  Hex_Digit_Display hex_digit_display_9 (.value(IM_Address[3:0]));  // open: dp
  and and_1 (and_1_out, B, not_1_out);
  LED led_1 (.in(N));
  LED led_2 (.in(Z));
  LED led_3 (.in(C));
  LED led_4 (.in(V));
  Multiplexer #(.width(12)) multiplexer_2 (
    .in0(multiplexer_3_out), .in1({3'b000, IM_Data[8:0]}), .out(multiplexer_2_out), .sel(and_1_out));
  Multiplexer #(.width(12)) multiplexer_3 (.in0(and_2_out), .in1({12{1'b0}}), .out(multiplexer_3_out), .sel(Reset));
  Register #(.width(12)) register_1 (
    .D(multiplexer_2_out), .en(1'b1), .clk(CLK), .Q({register_1_q, IM_Address}));  // open: clr
  twelveBitRCA twelvebitrca_1 (
    .M(1'b0), .A({register_1_q, IM_Address}), .B(12'h1), .R(twelvebitrca_1_r));  // open: Cout
  assign and_2_out = twelvebitrca_1_r & 12'h1ff;  // AND_Gate and_2, 12 bits wide

  // Other names for the same wires on the sheet: BTA[8:0] = IM_Data[8:0]; WS[1:0] = {MOVF, MOVC}

  // Notes on the sheet:
  //   Rd (0:2), Rn (5:3), Rm (8:6)
  //   This is the "write source" for the register. Bit 0 is set when constant, bit 1 is set when flags. See mux left of reg file
  //   Rn = RD1, Rm = RD2
  //   This is a mask for the lower 9 bits. Allows reuse of 12-bit circuitry
  //   (Overflow after 9th bit)
endmodule

module SignExtend6 (
  input  [5:0] S6,
  output [11:0] S12
);


  assign S12 = {{7{S6[5]}}, S6[4:0]};
endmodule

module FlagsReg (
  input  N,
  input  Z,
  input  C,
  input  V,
  input  [11:0] D12,
  input  NZW,
  input  CVW,
  input  FlagsW,
  input  CLK,
  input  Reset,
  output Nq,
  output Zq,
  output Cq,
  output Vq,
  output [11:0] Q12
);

  wire or_1_out, or_2_out;
  wire [1:0] multiplexer_1_out, multiplexer_2_out, multiplexer_3_out, multiplexer_4_out;

  Multiplexer #(.width(2)) multiplexer_1 (.in0({Z, N}), .in1(D12[1:0]), .out(multiplexer_1_out), .sel(FlagsW));
  Multiplexer #(.width(2)) multiplexer_2 (.in0({V, C}), .in1(D12[3:2]), .out(multiplexer_2_out), .sel(FlagsW));
  or or_1 (or_1_out, Reset, NZW);
  or or_2 (or_2_out, Reset, CVW);
  Multiplexer #(.width(2)) multiplexer_3 (.in0(multiplexer_1_out), .in1(2'b00), .out(multiplexer_3_out), .sel(Reset));
  Multiplexer #(.width(2)) multiplexer_4 (.in0(multiplexer_2_out), .in1(2'b00), .out(multiplexer_4_out), .sel(Reset));
  Register #(.width(2)) register_1 (.D(multiplexer_3_out), .en(or_1_out), .clk(CLK), .Q({Q12[1], Nq}), .clr(Reset));
  Register #(.width(2)) register_2 (.D(multiplexer_4_out), .en(or_2_out), .clk(CLK), .Q({Q12[3], Cq}), .clr(Reset));

  assign {Q12[11:4], Q12[2], Q12[0]} = {{8{1'b0}}, Cq, Nq};
  assign Vq = Q12[3];
  assign Zq = Q12[1];

  // Notes on the sheet:
  //   1st tier mux determines src, 2nd tier mux determines reset
endmodule

module ControlUnit (
  input  [11:0] IWord,
  output MOVC,
  output MOVF,
  output RegW,
  output FlagsW,
  output NZW,
  output CVW,
  output B,
  output [2:0] ALUOP
);

  wire and_1_out, and_2_out, and_3_out, decoder_1_out0, decoder_1_out1, decoder_1_out4, decoder_2_out1,
       decoder_2_out2, decoder_2_out5;
  wire [2:0] SubOp_out;

  Decoder #(.select(3)) decoder_1 (
    .out0(decoder_1_out0), .out1(decoder_1_out1), .out4(decoder_1_out4), .out6(MOVC), .out7(B),
    .sel(IWord[11:9]));  // open: out2, out3, out5, en
  Decoder #(.select(3)) decoder_2 (
    .out1(decoder_2_out1), .out2(decoder_2_out2), .out4(FlagsW), .out5(decoder_2_out5), .sel(IWord[8:6]));  // open: out0, out3, out6, out7, en
  and and_1 (and_1_out, decoder_1_out4, FlagsW);
  nor nor_1 (RegW, and_1_out, B);
  nor nor_2 (NZW, MOVC, B);
  and and_2 (and_2_out, decoder_1_out4, decoder_2_out2);
  and and_3 (and_3_out, decoder_1_out4, decoder_2_out1);
  and and_4 (MOVF, decoder_1_out4, decoder_2_out5);
  assign SubOp_out = IWord[11:9] | IWord[8:6];  // OR_Gate SubOp, 3 bits wide
  or or_1 (CVW, decoder_1_out0, decoder_1_out1, and_2_out, and_3_out);
  Multiplexer #(.width(3)) multiplexer_1 (.in0(IWord[11:9]), .in1(SubOp_out), .out(ALUOP), .sel(IWord[11]));

  // Other names for the same wires on the sheet: Rd[2:0] = IWord[2:0]; Rn[2:0] = IWord[5:3]; Rm[2:0] = IWord[8:6];
  //   Op[2:0] = IWord[11:9]

  // Notes on the sheet:
  //   Subop
  //   OR w/ subop works bc all possibilities are unutilized
  //   When op is 111, branch
endmodule

module fourBitCLA (
  input  [3:0] A,
  input  [3:0] B,
  input  M,
  output Cout,
  output [3:0] R
);

  wire A0B0_out, A1B1_out, A2B2_out, A3B3_out, and_1_out, and_2_out, and_3_out, and_4_out, and_5_out,
       and_6_out, and_7_out, and_8_out, and_9_out, and_10_out, C1_out, C2_out, C3_out, xor_1_out, xor_2_out,
       xor_3_out, xor_4_out;
  wire [3:0] multiplexer_1_out, not_1_out;

  Multiplexer #(.width(4)) multiplexer_1 (.in0(B), .in1(not_1_out), .out(multiplexer_1_out), .sel(M));
  assign not_1_out = ~B;  // NOT_Gate not_1, 4 bits wide
  and A0B0 (A0B0_out, multiplexer_1_out[0], A[0]);
  xor xor_1 (xor_1_out, multiplexer_1_out[3], A[3]);
  xor xor_2 (xor_2_out, multiplexer_1_out[2], A[2]);
  xor xor_3 (xor_3_out, multiplexer_1_out[1], A[1]);
  xor xor_4 (xor_4_out, multiplexer_1_out[0], A[0]);
  and A1B1 (A1B1_out, multiplexer_1_out[1], A[1]);
  and and_1 (and_1_out, M, xor_4_out, xor_3_out);
  and and_2 (and_2_out, A0B0_out, xor_3_out);
  and and_3 (and_3_out, M, xor_4_out);
  and A2B2 (A2B2_out, multiplexer_1_out[2], A[2]);
  and and_4 (and_4_out, M, xor_4_out, xor_3_out, xor_2_out);
  and and_5 (and_5_out, A0B0_out, xor_3_out, xor_2_out);
  and and_6 (and_6_out, A1B1_out, xor_2_out);
  or C2 (C2_out, A1B1_out, and_1_out, and_2_out);
  or C1 (C1_out, and_3_out, A0B0_out);
  and A3B3 (A3B3_out, multiplexer_1_out[3], A[3]);
  and and_7 (and_7_out, M, xor_4_out, xor_3_out, xor_2_out, xor_1_out);
  and and_8 (and_8_out, A0B0_out, xor_3_out, xor_2_out, xor_1_out);
  and and_9 (and_9_out, A1B1_out, xor_2_out, xor_1_out);
  and and_10 (and_10_out, A2B2_out, xor_1_out);
  or C3 (C3_out, A2B2_out, and_4_out, and_5_out, and_6_out);
  or C4 (Cout, A3B3_out, and_7_out, and_8_out, and_9_out, and_10_out);
  xor R3 (R[3], xor_1_out, C3_out);
  xor R2 (R[2], xor_2_out, C2_out);
  xor R1 (R[1], xor_3_out, C1_out);
  xor R0 (R[0], xor_4_out, M);

  // Notes on the sheet:
  //   Carry Bits
  //   Addition for R0-R3
endmodule

module twelveBitRCA (
  input  M,
  input  [11:0] A,
  input  [11:0] B,
  output Cout,
  output [11:0] R
);

  wire fourbitcla_1_cout, fourbitcla_2_cout, xor_1_out, xor_2_out;
  wire [3:0] multiplexer_1_out, multiplexer_2_out, not_1_out, not_2_out;

  fourBitCLA fourbitcla_1 (.A(A[3:0]), .B(B[3:0]), .M(M), .Cout(fourbitcla_1_cout), .R(R[3:0]));
  assign not_1_out = ~B[7:4];  // NOT_Gate not_1, 4 bits wide
  Multiplexer #(.width(4)) multiplexer_1 (.in0(B[7:4]), .in1(not_1_out), .out(multiplexer_1_out), .sel(xor_1_out));
  xor xor_1 (xor_1_out, fourbitcla_1_cout, M);
  fourBitCLA fourbitcla_2 (
    .A(A[7:4]), .B(multiplexer_1_out), .M(fourbitcla_1_cout), .Cout(fourbitcla_2_cout), .R(R[7:4]));
  assign not_2_out = ~B[11:8];  // NOT_Gate not_2, 4 bits wide
  xor xor_2 (xor_2_out, fourbitcla_2_cout, M);
  Multiplexer #(.width(4)) multiplexer_2 (.in0(B[11:8]), .in1(not_2_out), .out(multiplexer_2_out), .sel(xor_2_out));
  fourBitCLA fourbitcla_3 (.A(A[11:8]), .B(multiplexer_2_out), .M(fourbitcla_2_cout), .Cout(Cout), .R(R[11:8]));

  // Notes on the sheet:
  //   A3-A0 & B3-B0
  //   I have to invert the value of every 4 bits of B to invert the subtraction to use only one input for Mode/Carry in. Otherwise, this is a simple ripple-carry adder.
  //   A7-A4 & B7-B4
  //   A11-A8 & B11-B8
endmodule

module dLatch (
  input  CLK,
  input  D,
  output Q,
  output QNot
);

  wire and_1_out, and_2_out, not_1_out;

  not not_1 (not_1_out, D);
  and and_1 (and_1_out, CLK, not_1_out);
  and and_2 (and_2_out, CLK, D);
  nor nor_1 (Q, and_1_out, QNot);
  nor nor_2 (QNot, Q, and_2_out);

  // Notes on the sheet:
  //   This is the simplest building block of the Register
endmodule

module dFlipFlop (
  input  CLK,
  input  D,
  output Q,
  output QNot
);

  wire dlatch_1_q, not_1_out;

  not not_1 (not_1_out, CLK);
  dLatch dlatch_1 (.CLK(not_1_out), .D(D), .Q(dlatch_1_q));  // open: QNot
  dLatch dlatch_2 (.CLK(CLK), .D(dlatch_1_q), .Q(Q), .QNot(QNot));

  // Notes on the sheet:
  //   This latch ensures it only gets set on clock edge
endmodule

module twelveBitRegister (
  input  WE,
  input  CLK,
  input  [11:0] D,
  output [11:0] Q
);

  wire and_1_out;

  and and_1 (and_1_out, WE, CLK);
  dFlipFlop dflipflop_1 (.CLK(and_1_out), .D(D[11]), .Q(Q[11]));  // open: QNot
  dFlipFlop dflipflop_2 (.CLK(and_1_out), .D(D[10]), .Q(Q[10]));  // open: QNot
  dFlipFlop dflipflop_3 (.CLK(and_1_out), .D(D[9]), .Q(Q[9]));  // open: QNot
  dFlipFlop dflipflop_4 (.CLK(and_1_out), .D(D[8]), .Q(Q[8]));  // open: QNot
  dFlipFlop dflipflop_5 (.CLK(and_1_out), .D(D[7]), .Q(Q[7]));  // open: QNot
  dFlipFlop dflipflop_6 (.CLK(and_1_out), .D(D[6]), .Q(Q[6]));  // open: QNot
  dFlipFlop dflipflop_7 (.CLK(and_1_out), .D(D[5]), .Q(Q[5]));  // open: QNot
  dFlipFlop dflipflop_8 (.CLK(and_1_out), .D(D[4]), .Q(Q[4]));  // open: QNot
  dFlipFlop dflipflop_9 (.CLK(and_1_out), .D(D[3]), .Q(Q[3]));  // open: QNot
  dFlipFlop dflipflop_10 (.CLK(and_1_out), .D(D[2]), .Q(Q[2]));  // open: QNot
  dFlipFlop dflipflop_11 (.CLK(and_1_out), .D(D[1]), .Q(Q[1]));  // open: QNot
  dFlipFlop dflipflop_12 (.CLK(and_1_out), .D(D[0]), .Q(Q[0]));  // open: QNot

  // Notes on the sheet:
  //   This is simply 12 flip flops that are only written to when Write Enable (WE) and CLK are both true
endmodule

module twoBitRegister (
  input  WE,
  input  CLK,
  input  [1:0] D,
  output [1:0] Q
);

  wire and_1_out;

  and and_1 (and_1_out, WE, CLK);
  dFlipFlop R1 (.CLK(and_1_out), .D(D[1]), .Q(Q[1]));  // open: QNot
  dFlipFlop R0 (.CLK(and_1_out), .D(D[0]), .Q(Q[0]));  // open: QNot
endmodule
